// Digital circuit Seta.dig as structural Verilog
module Seta (
  input  clk
);

  wire Botao_Seta_Direita_out, Botao_Seta_Esquerda_out, resposta_1_saida_seta, resposta_2_saida_seta;

  LED Seta_Esquerda (.in(resposta_1_saida_seta));
  resposta resposta_1 (.clk(clk), .Btn_Seta(Botao_Seta_Esquerda_out), .Saida_Seta(resposta_1_saida_seta));
  DipSwitch Botao_Seta_Esquerda (.out(Botao_Seta_Esquerda_out));
  DipSwitch Botao_Seta_Direita (.out(Botao_Seta_Direita_out));
  resposta resposta_2 (.clk(clk), .Btn_Seta(Botao_Seta_Direita_out), .Saida_Seta(resposta_2_saida_seta));
  LED Seta_Direita (.in(resposta_2_saida_seta));

  // Notes on the sheet:
  //   Esse eh o circuito principal que sera usado para testes. Nao edite.
endmodule
