// Digital circuit resposta.dig as structural Verilog
module resposta (
  input  clk,
  input  Btn_Seta,
  output Saida_Seta
);

  wire and_1_out, and_2_out, and_3_out, and_4_out, and_5_out, and_6_out, and_7_out, and_8_out, and_9_out,
       E1_q, E2_q, or_1_out, or_2_out, or_3_out;

  and and_1 (and_1_out, E2_q, ~Saida_Seta, ~Btn_Seta);  // And
  and and_2 (and_2_out, ~E1_q, Saida_Seta, ~Btn_Seta);  // And
  and and_3 (and_3_out, E2_q, ~E1_q, Saida_Seta, ~Btn_Seta);  // And
  and and_4 (and_4_out, ~E2_q, Saida_Seta, Btn_Seta);  // And
  and and_5 (and_5_out, ~E2_q, E1_q, Btn_Seta);  // And
  and and_6 (and_6_out, E2_q, E1_q, ~Saida_Seta, ~Btn_Seta);  // And
  and and_7 (and_7_out, E2_q, ~Saida_Seta);  // And
  and and_8 (and_8_out, E2_q, Btn_Seta);
  and and_9 (and_9_out, ~Saida_Seta, Btn_Seta);  // And
  or or_1 (or_1_out, and_1_out, and_2_out);
  or or_2 (or_2_out, and_3_out, and_4_out, and_5_out, and_6_out);
  or or_3 (or_3_out, and_7_out, and_8_out, and_9_out);
  D_FF E2 (.D(or_1_out), .C(clk), .Q(E2_q));  // open: nQ
  D_FF E1 (.D(or_2_out), .C(clk), .Q(E1_q));  // open: nQ
  D_FF E0 (.D(or_3_out), .C(clk), .Q(Saida_Seta));  // open: nQ
endmodule
