// Logisim project somador-subtrator.circ as structural Verilog: 5 circuits, main circuit AND
module main (
  input  A7,
  input  A6,
  input  A5,
  input  A4,
  input  A3,
  input  A2,
  input  A1,
  input  A0,
  input  B7,
  input  B6,
  input  B5,
  input  B4,
  input  B3,
  input  B2,
  input  B1,
  input  B0,
  input  Operacao,
  output Overflow,
  output S7,
  output S6,
  output S5,
  output S4,
  output S3,
  output S2,
  output S1,
  output S0
);

  Somador somador_1 (
    .A7(A7), .A6(A6), .B7(B7), .B6(B6), .A5(A5), .B5(B5), .A4(A4), .B4(B4), .A3(A3), .B3(B3), .A2(A2),
    .B2(B2), .B1(B1), .A1(A1), .B0(B0), .A0(A0), .Operacao(Operacao), .Overflow(Overflow), .S7(S7), .S6(S6),
    .S5(S5), .S4(S4), .S3(S3), .S2(S2), .S1(S1), .S0(S0));

  // Notes on the sheet:
  //   Nao edite o main. Voce deve implementar no circuito somador.
endmodule

module Somador (
  input  B7,
  input  B6,
  input  B5,
  input  B4,
  input  B3,
  input  B2,
  input  B1,
  input  B0,
  input  Operacao,
  input  A7,
  input  A6,
  input  A5,
  input  A4,
  input  A3,
  input  A2,
  input  A1,
  input  A0,
  output Overflow,
  output S7,
  output S6,
  output S5,
  output S4,
  output S3,
  output S2,
  output S1,
  output S0
);

  wire and_1_s, and_3_s, and_4_s, and_5_s, and_6_s, and_7_s, and_8_s, and_9_s, and_10_s, and_11_s, and_12_s,
       and_13_s, and_14_s, and_15_s, and_16_s, and_17_s, and_18_s, and_19_s, and_20_s, and_21_s, and_22_s,
       and_23_s, and_24_s, and_25_s, and_26_s, and_27_s, and_28_s, and_29_s, and_30_s, and_31_s, and_32_s,
       and_33_s, and_34_s, and_35_s, and_36_s, and_37_s, and_38_s, and_39_s, and_40_s, and_41_s, and_42_s,
       and_43_s, and_44_s, mux_1_f, mux_2_f, mux_3_f, mux_4_f, mux_5_f, mux_6_f, mux_7_f, mux_8_f,
       nand_1_out, nand_2_out, nand_3_out, nand_4_out, nand_5_out, nand_6_out, nand_7_out, nand_8_out,
       xor_1_s, xor_2_s, xor_3_s, xor_4_s, xor_5_s, xor_6_s, xor_7_s, xor_8_s, xor_9_s, xor_10_s, xor_12_s,
       xor_13_s, xor_14_s, xor_15_s, xor_16_s, xor_17_s, xor_18_s, xor_20_s, xor_21_s, xor_22_s, xor_23_s,
       xor_24_s, xor_25_s, xor_27_s, xor_28_s, xor_29_s, xor_30_s, xor_31_s, xor_33_s, xor_34_s, xor_35_s,
       xor_36_s, xor_38_s, xor_39_s, xor_40_s, xor_41_s, xor_43_s, xor_44_s, xor_45_s, xor_47_s, xor_48_s,
       xor_50_s;

  AND and_1 (.A(mux_1_f), .B(A7), .S(and_1_s));
  XOR xor_1 (.A(and_3_s), .B(and_1_s), .S(xor_1_s));
  XOR xor_2 (.A(and_4_s), .B(xor_1_s), .S(xor_2_s));
  XOR xor_3 (.A(and_5_s), .B(xor_2_s), .S(xor_3_s));
  XOR xor_4 (.A(and_6_s), .B(xor_3_s), .S(xor_4_s));
  XOR xor_5 (.A(and_7_s), .B(xor_4_s), .S(xor_5_s));
  nand nand_1 (nand_1_out, B7, B7);
  AND and_2 (.A(and_10_s), .B(nand_1_out));  // open: S
  MUX mux_1 (.A(xor_12_s), .S(Operacao), .B(B7), .F(mux_1_f));
  XOR xor_6 (.A(mux_1_f), .B(A7), .S(xor_6_s));
  AND and_3 (.A(and_11_s), .B(xor_6_s), .S(and_3_s));
  XOR xor_7 (.A(and_11_s), .B(xor_6_s), .S(xor_7_s));
  AND and_4 (.A(and_12_s), .B(xor_7_s), .S(and_4_s));
  XOR xor_8 (.A(and_12_s), .B(xor_7_s), .S(xor_8_s));
  AND and_5 (.A(and_13_s), .B(xor_8_s), .S(and_5_s));
  XOR xor_9 (.A(and_13_s), .B(xor_8_s), .S(xor_9_s));
  AND and_6 (.A(and_14_s), .B(xor_9_s), .S(and_6_s));
  AND and_7 (.A(and_15_s), .B(xor_16_s), .S(and_7_s));
  AND and_8 (.A(and_16_s), .B(xor_17_s), .S(and_8_s));
  XOR xor_10 (.A(and_8_s), .B(xor_5_s), .S(xor_10_s));
  AND and_9 (.A(and_17_s), .B(xor_18_s), .S(and_9_s));
  XOR xor_11 (.A(and_9_s), .B(xor_10_s), .S(Overflow));
  AND and_10 (.A(and_18_s), .B(nand_2_out), .S(and_10_s));
  XOR xor_12 (.A(and_10_s), .B(nand_1_out), .S(xor_12_s));
  MUX mux_2 (.A(xor_20_s), .S(Operacao), .B(B6), .F(mux_2_f));
  AND and_11 (.A(mux_2_f), .B(A6), .S(and_11_s));
  XOR xor_13 (.A(mux_2_f), .B(A6), .S(xor_13_s));
  AND and_12 (.A(and_19_s), .B(xor_13_s), .S(and_12_s));
  XOR xor_14 (.A(and_19_s), .B(xor_13_s), .S(xor_14_s));
  AND and_13 (.A(and_20_s), .B(xor_14_s), .S(and_13_s));
  XOR xor_15 (.A(and_20_s), .B(xor_14_s), .S(xor_15_s));
  AND and_14 (.A(and_21_s), .B(xor_15_s), .S(and_14_s));
  AND and_15 (.A(and_22_s), .B(xor_23_s), .S(and_15_s));
  XOR xor_16 (.A(and_14_s), .B(xor_9_s), .S(xor_16_s));
  AND and_16 (.A(and_23_s), .B(xor_24_s), .S(and_16_s));
  XOR xor_17 (.A(and_15_s), .B(xor_16_s), .S(xor_17_s));
  AND and_17 (.A(and_24_s), .B(xor_25_s), .S(and_17_s));
  XOR xor_18 (.A(and_16_s), .B(xor_17_s), .S(xor_18_s));
  XOR xor_19 (.A(and_17_s), .B(xor_18_s), .S(S7));
  nand nand_2 (nand_2_out, B6, B6);
  AND and_18 (.A(and_25_s), .B(nand_3_out), .S(and_18_s));
  XOR xor_20 (.A(and_18_s), .B(nand_2_out), .S(xor_20_s));
  MUX mux_3 (.A(xor_27_s), .S(Operacao), .B(B5), .F(mux_3_f));
  AND and_19 (.A(mux_3_f), .B(A5), .S(and_19_s));
  XOR xor_21 (.A(mux_3_f), .B(A5), .S(xor_21_s));
  AND and_20 (.A(and_26_s), .B(xor_21_s), .S(and_20_s));
  XOR xor_22 (.A(and_26_s), .B(xor_21_s), .S(xor_22_s));
  AND and_21 (.A(and_27_s), .B(xor_22_s), .S(and_21_s));
  AND and_22 (.A(and_28_s), .B(xor_29_s), .S(and_22_s));
  XOR xor_23 (.A(and_21_s), .B(xor_15_s), .S(xor_23_s));
  AND and_23 (.A(and_29_s), .B(xor_30_s), .S(and_23_s));
  XOR xor_24 (.A(and_22_s), .B(xor_23_s), .S(xor_24_s));
  AND and_24 (.A(and_30_s), .B(xor_31_s), .S(and_24_s));
  XOR xor_25 (.A(and_23_s), .B(xor_24_s), .S(xor_25_s));
  XOR xor_26 (.A(and_24_s), .B(xor_25_s), .S(S6));
  nand nand_3 (nand_3_out, B5, B5);
  AND and_25 (.A(and_31_s), .B(nand_4_out), .S(and_25_s));
  XOR xor_27 (.A(and_25_s), .B(nand_3_out), .S(xor_27_s));
  AND and_26 (.A(mux_4_f), .B(A4), .S(and_26_s));
  XOR xor_28 (.A(mux_4_f), .B(A4), .S(xor_28_s));
  AND and_27 (.A(and_32_s), .B(xor_28_s), .S(and_27_s));
  AND and_28 (.A(and_33_s), .B(xor_34_s), .S(and_28_s));
  XOR xor_29 (.A(and_27_s), .B(xor_22_s), .S(xor_29_s));
  AND and_29 (.A(and_34_s), .B(xor_35_s), .S(and_29_s));
  XOR xor_30 (.A(and_28_s), .B(xor_29_s), .S(xor_30_s));
  AND and_30 (.A(and_35_s), .B(xor_36_s), .S(and_30_s));
  XOR xor_31 (.A(and_29_s), .B(xor_30_s), .S(xor_31_s));
  XOR xor_32 (.A(and_30_s), .B(xor_31_s), .S(S5));
  nand nand_4 (nand_4_out, B4, B4);
  AND and_31 (.A(and_39_s), .B(nand_5_out), .S(and_31_s));
  XOR xor_33 (.A(and_31_s), .B(nand_4_out), .S(xor_33_s));
  MUX mux_4 (.A(xor_33_s), .S(Operacao), .B(B4), .F(mux_4_f));
  AND and_32 (.A(mux_5_f), .B(A3), .S(and_32_s));
  AND and_33 (.A(and_36_s), .B(xor_39_s), .S(and_33_s));
  XOR xor_34 (.A(and_32_s), .B(xor_28_s), .S(xor_34_s));
  AND and_34 (.A(and_37_s), .B(xor_40_s), .S(and_34_s));
  XOR xor_35 (.A(and_33_s), .B(xor_34_s), .S(xor_35_s));
  AND and_35 (.A(and_38_s), .B(xor_41_s), .S(and_35_s));
  XOR xor_36 (.A(and_34_s), .B(xor_35_s), .S(xor_36_s));
  XOR xor_37 (.A(and_35_s), .B(xor_36_s), .S(S4));
  nand nand_5 (nand_5_out, B3, B3);
  XOR xor_38 (.A(and_39_s), .B(nand_5_out), .S(xor_38_s));
  MUX mux_5 (.A(xor_38_s), .S(Operacao), .B(B3), .F(mux_5_f));
  AND and_36 (.A(mux_6_f), .B(A2), .S(and_36_s));
  XOR xor_39 (.A(mux_5_f), .B(A3), .S(xor_39_s));
  AND and_37 (.A(and_40_s), .B(xor_44_s), .S(and_37_s));
  XOR xor_40 (.A(and_36_s), .B(xor_39_s), .S(xor_40_s));
  AND and_38 (.A(and_41_s), .B(xor_45_s), .S(and_38_s));
  XOR xor_41 (.A(and_37_s), .B(xor_40_s), .S(xor_41_s));
  XOR xor_42 (.A(and_38_s), .B(xor_41_s), .S(S3));
  nand nand_6 (nand_6_out, B2, B2);
  AND and_39 (.A(and_42_s), .B(nand_6_out), .S(and_39_s));
  XOR xor_43 (.A(and_42_s), .B(nand_6_out), .S(xor_43_s));
  MUX mux_6 (.A(xor_43_s), .S(Operacao), .B(B2), .F(mux_6_f));
  AND and_40 (.A(mux_7_f), .B(A1), .S(and_40_s));
  XOR xor_44 (.A(mux_6_f), .B(A2), .S(xor_44_s));
  AND and_41 (.A(and_43_s), .B(xor_48_s), .S(and_41_s));
  XOR xor_45 (.A(and_40_s), .B(xor_44_s), .S(xor_45_s));
  XOR xor_46 (.A(and_41_s), .B(xor_45_s), .S(S2));
  nand nand_7 (nand_7_out, B1, B1);
  AND and_42 (.A(and_44_s), .B(nand_7_out), .S(and_42_s));
  XOR xor_47 (.A(and_44_s), .B(nand_7_out), .S(xor_47_s));
  MUX mux_7 (.A(xor_47_s), .S(Operacao), .B(B1), .F(mux_7_f));
  AND and_43 (.A(mux_8_f), .B(A0), .S(and_43_s));
  XOR xor_48 (.A(mux_7_f), .B(A1), .S(xor_48_s));
  XOR xor_49 (.A(and_43_s), .B(xor_48_s), .S(S1));
  nand nand_8 (nand_8_out, B0, B0);
  AND and_44 (.A(Operacao), .B(nand_8_out), .S(and_44_s));
  XOR xor_50 (.A(Operacao), .B(nand_8_out), .S(xor_50_s));
  MUX mux_8 (.A(xor_50_s), .S(Operacao), .B(B0), .F(mux_8_f));
  XOR xor_51 (.A(mux_8_f), .B(A0), .S(S0));
endmodule

module XOR (
  input  A,
  input  B,
  output S
);

  wire nand_1_out, nand_2_out, nand_3_out;

  nand nand_1 (nand_1_out, A, B);
  nand nand_2 (nand_2_out, A, nand_1_out);
  nand nand_3 (nand_3_out, nand_1_out, B);
  nand nand_4 (S, nand_2_out, nand_3_out);
endmodule

module AND (
  input  A,
  input  B,
  output S
);

  wire nand_1_out;

  nand nand_1 (nand_1_out, A, B);
  nand nand_2 (S, nand_1_out, nand_1_out);
endmodule

module MUX (
  input  A,
  input  S,
  input  B,
  output F
);

  wire nand_1_out, nand_2_out, nand_3_out;

  nand nand_1 (nand_1_out, S, S);
  nand nand_2 (nand_2_out, A, S);
  nand nand_3 (nand_3_out, nand_1_out, B);
  nand nand_4 (F, nand_2_out, nand_3_out);
endmodule
